# Fritzing sketch turret (saved by Fritzing 0.7.10b)
breadboards: 1

parts:
  Arduino1 = Arduino
  J1 = Basic Servo
  M1 = DC Motor
  M2 = DC Motor
  M3 = DC Motor
  M4 = DC Motor
  Q1 = NPN-Transistor [package="TO92 [THT]"]
  IC1 = H-Bridge [package=THT]
  D1 = Rectifier Diode [part_number=1N4001 package="300 mil [THT]"]
  S6 = Toggle Switch [package=THT]
  S7 = Toggle Switch [package=THT]
  S8 = Toggle Switch [package=THT]
  S9 = Toggle Switch [package=THT]
  U1 = mystery part, 4 pins [chip_label=Wii]
  R1 = Resistor [tolerance=±5% resistance=8k package=THT]
  R2 = Resistor [tolerance=±5% resistance=8k package=THT]
  R3 = Resistor [tolerance=±5% resistance=8k package=THT]
  R4 = Resistor [tolerance=±5% resistance=8k package=THT]
  R5 = Resistor [tolerance=±5% resistance=220 package=THT]

nets:
  GND: Arduino1.GND, J1.gnd, M1.pin_2, M2.pin_2, IC1.GND1, IC1.GND2, IC1.GND3, IC1.GND4, S6.L2, S7.L2, S8.L2, S9.L2, U1.pin1
  N1: Arduino1.D13, IC1.1A
  N2: Arduino1.D12, IC1.2A
  N3: Arduino1.D11, IC1.1_2EN
  N4: Arduino1.D10, IC1.3_4EN
  N5: Arduino1.D9, IC1.4A
  N6: Arduino1.D8, IC1.3A
  N7: Arduino1.D7, S8.COM
  N8: Arduino1.D6, S6.COM
  N9: Arduino1.D5, S7.COM
  N10: Arduino1.D4, S9.COM
  N11: Arduino1.D3, J1.pulse
  N12: Arduino1.D2, R5.Pin_0
  3.3V: Arduino1.3V3
  5V: Arduino1.+5V, J1.vcc, IC1.VCC1, U1.pin4, R1.Pin_0, R2.Pin_0, R3.Pin_0, R4.Pin_0
  12V: Arduino1.VIN, Q1.C, IC1.VCC2
  N13: Arduino1.A4, U1.pin3
  N14: Arduino1.A5, U1.pin2
  N15: M1.pin_1, M2.pin_1, D1.cathode
  N16: M3.pin_1, IC1.2Y
  N17: M3.pin_2, IC1.1Y
  N18: M4.pin_1, IC1.4Y
  N19: M4.pin_2, IC1.3Y
  N20: Q1.E, D1.anode
  N21: Q1.B, R5.Pin_1
  N22: S6.L1, R2.Pin_1
  N23: S7.L1, R3.Pin_1
  N24: S8.L1, R1.Pin_1
  N25: S9.L1, R4.Pin_1

notes:
  Trigger lever
  Nerf motors
  Position switches
  Azimuth motor
  Elevation motor
